// Logisim project a2q2(EFlannery).circ as structural Verilog: 6 circuits, main circuit Main (A2Q2 Flannery)
module Main__A2Q2_Flannery (
  input  [7:0] Multiplicand,
  input  [7:0] Multiplier,
  input  Reset,
  output DONE,
  output [15:0] Product
);

  wire adder_1_cout, Control_load_carry, Control_load_mult, Control_load_multip, Control_load_sum,
       Control_shift, CPM_least_sig_bit;
  wire [7:0] adder_1_out, multiplexer_1_out, Multiplic_multipli__out;

  // Probe on Product
  // Probe on Multiplier
  Carry_Product_Multiplier__A2Q2_Flannery CPM (
    .Load_Multiplier(Control_load_multip), .Load_Sum(Control_load_sum), .Shift(Control_shift),
    .Carry(adder_1_cout), .Reset(Reset), .Sum(adder_1_out), .Multiplier(Multiplier),
    .Least_Sig_Bit(CPM_least_sig_bit), .Sum_Output(Product[15:8]), .Multiplier_Output(Product[7:0]),
    .Load_Carry(Control_load_carry));
  Multiplicand__A2Q2_Flannery Multiplic (
    .Multiplicand(Multiplicand), .Load_IN(Control_load_mult), .Reset(Reset),
    .Multipli__OUT(Multiplic_multipli__out));
  Multiplexer #(.width(8)) multiplexer_1 (
    .in0({8{1'b0}}), .in1(Multiplic_multipli__out), .out(multiplexer_1_out), .sel(CPM_least_sig_bit));  // open: en
  Adder adder_1 (.a(multiplexer_1_out), .b(Product[15:8]), .out(adder_1_out), .cout(adder_1_cout));  // open: cin
  // Probe on Multiplicand
  Control__A2Q2_Flannery Control (
    .Reset(Reset), .Load_Mult(Control_load_mult), .Load_Multip(Control_load_multip),
    .Load_Sum(Control_load_sum), .Load_Carry(Control_load_carry), .Shift(Control_shift), .Done(DONE));

  // Notes on the sheet:
  //   Elizabeth Flannery
  //   260406383
  //   COMP274: A2 Q2
endmodule

module Control__A2Q2_Flannery (
  input  Reset,
  output Load_Mult,
  output Load_Multip,
  output Load_Sum,
  output Load_Carry,
  output Shift,
  output Done
);

  wire clock_1_out, counter_1_carry, next_state_a2q2_flannery_1_state_0, next_state_a2q2_flannery_1_state_1,
       next_state_a2q2_flannery_1_state_2, next_state_a2q2_flannery_1_state_3,
       output_a2q2_flannery_1_counter_plus_plus, STATE_0_q, STATE_1_q, STATE_2_q, STATE_3_q;

  Clock clock_1 (.out(clock_1_out));
  Next_State__A2Q2_Flannery next_state_a2q2_flannery_1 (
    .Reset(Reset), .State_0_IN(STATE_0_q), .State_1_IN(STATE_1_q), .State_2_IN(STATE_2_q),
    .State_3_IN(STATE_3_q), .Counter_Carry(counter_1_carry), .State_0(next_state_a2q2_flannery_1_state_0),
    .State_1(next_state_a2q2_flannery_1_state_1), .State_2(next_state_a2q2_flannery_1_state_2),
    .State_3(next_state_a2q2_flannery_1_state_3));
  D_Flip_Flop STATE_0 (
    .clk(clock_1_out), .D(next_state_a2q2_flannery_1_state_0), .Q(STATE_0_q));  // open: Qn, preset, en, reset
  D_Flip_Flop STATE_1 (
    .clk(clock_1_out), .D(next_state_a2q2_flannery_1_state_1), .Q(STATE_1_q));  // open: Qn, preset, en, reset
  D_Flip_Flop STATE_2 (
    .clk(clock_1_out), .D(next_state_a2q2_flannery_1_state_2), .Q(STATE_2_q));  // open: Qn, preset, en, reset
  D_Flip_Flop STATE_3 (
    .clk(clock_1_out), .D(next_state_a2q2_flannery_1_state_3), .Q(STATE_3_q));  // open: Qn, preset, en, reset
  Counter #(.width(3), .max('h7)) counter_1 (
    .count(output_a2q2_flannery_1_counter_plus_plus), .carry(counter_1_carry), .clk(clock_1_out));  // open: load, D, Q, clr
  Output__A2Q2_Flannery output_a2q2_flannery_1 (
    .State_0(STATE_0_q), .State_1(STATE_1_q), .State_2(STATE_2_q), .State_3(STATE_3_q),
    .Load_Mult(Load_Mult), .Load_Multip(Load_Multip), .Load_Sum(Load_Sum), .Load_Carry(Load_Carry),
    .Shift(Shift), .Counter_plus_plus(output_a2q2_flannery_1_counter_plus_plus), .Done(Done));
endmodule

module Next_State__A2Q2_Flannery (
  input  Reset,
  input  State_0_IN,
  input  State_1_IN,
  input  State_2_IN,
  input  State_3_IN,
  input  Counter_Carry,
  output State_0,
  output State_1,
  output State_2,
  output State_3
);

  wire and_1_out, and_3_out, and_4_out, and_5_out, not_1_out;

  not not_1 (not_1_out, Reset);
  and and_1 (and_1_out, State_0_IN, not_1_out);
  and and_2 (State_2, State_1_IN, not_1_out);
  and and_3 (and_3_out, State_2_IN, not_1_out, ~Counter_Carry);  // AND_Gate
  and and_4 (and_4_out, State_3_IN, not_1_out);
  and and_5 (and_5_out, State_2_IN, not_1_out, Counter_Carry);
  or or_1 (State_1, and_1_out, and_3_out);
  or or_2 (State_3, and_5_out, and_4_out);

  assign State_0 = Reset;
endmodule

module Output__A2Q2_Flannery (
  input  State_0,
  input  State_1,
  input  State_2,
  input  State_3,
  output Load_Mult,
  output Load_Multip,
  output Load_Sum,
  output Load_Carry,
  output Shift,
  output Counter_plus_plus,
  output Done
);


  assign Counter_plus_plus = State_2;
  assign Done = State_3;
  assign Load_Carry = State_1;
  assign Load_Mult = State_0;
  assign Load_Multip = State_0;
  assign Load_Sum = State_1;
  assign Shift = State_2;
endmodule

module Multiplicand__A2Q2_Flannery (
  input  [7:0] Multiplicand,
  input  Load_IN,
  input  Reset,
  output [7:0] Multipli__OUT
);

  wire clock_1_out;

  Clock clock_1 (.out(clock_1_out));
  Register register_1 (.D(Multiplicand), .en(Load_IN), .Q(Multipli__OUT), .clk(clock_1_out), .clr(Reset));
endmodule

module Carry_Product_Multiplier__A2Q2_Flannery (
  input  Load_Multiplier,
  input  [7:0] Sum,
  input  [7:0] Multiplier,
  input  Load_Sum,
  input  Shift,
  input  Carry,
  input  Reset,
  input  Load_Carry,
  output Least_Sig_Bit,
  output [7:0] Sum_Output,
  output [7:0] Multiplier_Output
);

  wire clock_1_out, d_ff_1_q, shift_register_1_out;

  Shift_Register shift_register_1 (
    .shift(Shift), .in(d_ff_1_q), .clk(clock_1_out), .out(shift_register_1_out), .load(Load_Sum),
    .clr(Reset), .d0(Sum[7]), .q0(Sum_Output[7]), .d1(Sum[6]), .q1(Sum_Output[6]), .d2(Sum[5]),
    .q2(Sum_Output[5]), .d3(Sum[4]), .q3(Sum_Output[4]), .d4(Sum[3]), .q4(Sum_Output[3]), .d5(Sum[2]),
    .q5(Sum_Output[2]), .d6(Sum[1]), .q6(Sum_Output[1]), .d7(Sum[0]), .q7(Sum_Output[0]));
  D_Flip_Flop d_ff_1 (.clk(clock_1_out), .D(Carry), .Q(d_ff_1_q), .en(Load_Carry), .reset(Reset));  // open: Qn, preset
  Clock clock_1 (.out(clock_1_out));
  Shift_Register shift_register_2 (
    .shift(Shift), .in(shift_register_1_out), .clk(clock_1_out), .load(Load_Multiplier), .clr(Reset),
    .d0(Multiplier[7]), .q0(Multiplier_Output[7]), .d1(Multiplier[6]), .q1(Multiplier_Output[6]),
    .d2(Multiplier[5]), .q2(Multiplier_Output[5]), .d3(Multiplier[4]), .q3(Multiplier_Output[4]),
    .d4(Multiplier[3]), .q4(Multiplier_Output[3]), .d5(Multiplier[2]), .q5(Multiplier_Output[2]),
    .d6(Multiplier[1]), .q6(Multiplier_Output[1]), .d7(Multiplier[0]), .q7(Least_Sig_Bit));  // open: out

  assign Multiplier_Output[0] = Least_Sig_Bit;
endmodule
