// Logisim project a2q3(EFlannery).circ as structural Verilog: 7 circuits, main circuit Main
module Main (
  input  [7:0] Divisor,
  input  Reset,
  input  [7:0] Dividend,
  output [7:0] Remainder,
  output DONE,
  output [7:0] Quotient_Output
);

  wire control_1_load_dividend_into_q, control_1_load_divisor, control_1_q_shift_in__neg, control_1_shift_q,
       control_1_shift_remainder, control_1_write_sub_into_r, subtractor_1_bout;
  wire [7:0] divisor_1_divisor_out, subtractor_1_out;

  // Probe on Remainder
  // Probe on Quotient_Output
  // Probe on Dividend
  Div_Rem div_rem_1 (
    .Dividend(Dividend), .Shift_Q(control_1_shift_q), .Q_Shift_In(control_1_q_shift_in__neg),
    .Load_Div_into_Q(control_1_load_dividend_into_q), .Quotient(Quotient_Output),
    .Write_Sub_to_R(control_1_write_sub_into_r), .Reset(Reset), .Sub(subtractor_1_out),
    .Shift_R(control_1_shift_remainder), .Remainder(Remainder));
  // Probe on Divisor
  Divisor divisor_1 (
    .Divisor(Divisor), .Load_IN(control_1_load_divisor), .Reset(Reset), .Divisor_OUT(divisor_1_divisor_out));
  Subtractor subtractor_1 (
    .a(Remainder), .b(divisor_1_divisor_out), .out(subtractor_1_out), .bout(subtractor_1_bout));  // open: bin
  Control control_1 (
    .Neg(subtractor_1_bout), .Reset(Reset), .Load_Divisor(control_1_load_divisor),
    .Load_Dividend_into_Q(control_1_load_dividend_into_q), .Write_Sub_into_R(control_1_write_sub_into_r),
    .Q_Shift_In__Neg(control_1_q_shift_in__neg), .Shift_Q(control_1_shift_q),
    .Shift_Remainder(control_1_shift_remainder), .Done(DONE));

  // Notes on the sheet:
  //   Elizabeth Flannery
  //   260406383
  //   COMP274 A2 Q3
endmodule

module Divisor (
  input  [7:0] Divisor,
  input  Load_IN,
  input  Reset,
  output [7:0] Divisor_OUT
);

  wire clock_1_out;

  Clock clock_1 (.out(clock_1_out));
  Register register_1 (.D(Divisor), .en(Load_IN), .Q(Divisor_OUT), .clk(clock_1_out), .clr(Reset));
endmodule

module Control (
  input  Reset,
  input  Neg,
  output Load_Divisor,
  output Load_Dividend_into_Q,
  output Write_Sub_into_R,
  output Q_Shift_In__Neg,
  output Shift_Q,
  output Shift_Remainder,
  output Done
);

  wire clock_1_out, counter_1_carry, next_state_1_state_0, next_state_1_state_1, next_state_1_state_2,
       next_state_1_state_3, output_1_counter_plus_plus, STATE_0_q, STATE_1_q, STATE_2_q, STATE_3_q;

  Clock clock_1 (.out(clock_1_out));
  Next_State next_state_1 (
    .Reset(Reset), .State_0_IN(STATE_0_q), .State_1_IN(STATE_1_q), .State_2_IN(STATE_2_q),
    .State_3_IN(STATE_3_q), .Counter_Carry(counter_1_carry), .State_0(next_state_1_state_0),
    .State_1(next_state_1_state_1), .State_2(next_state_1_state_2), .State_3(next_state_1_state_3));
  D_Flip_Flop STATE_0 (.clk(clock_1_out), .D(next_state_1_state_0), .Q(STATE_0_q));  // open: Qn, preset, en, reset
  D_Flip_Flop STATE_1 (.clk(clock_1_out), .D(next_state_1_state_1), .Q(STATE_1_q));  // open: Qn, preset, en, reset
  D_Flip_Flop STATE_2 (.clk(clock_1_out), .D(next_state_1_state_2), .Q(STATE_2_q));  // open: Qn, preset, en, reset
  D_Flip_Flop STATE_3 (.clk(clock_1_out), .D(next_state_1_state_3), .Q(STATE_3_q));  // open: Qn, preset, en, reset
  Counter #(.width(4), .max('h8)) counter_1 (
    .count(output_1_counter_plus_plus), .carry(counter_1_carry), .clk(clock_1_out));  // open: load, D, Q, clr
  Output output_1 (
    .State_0(STATE_0_q), .State_1(STATE_1_q), .State_2(STATE_2_q), .Count_Carry(counter_1_carry),
    .State_3(STATE_3_q), .Neg(Neg), .Load_Divisor(Load_Divisor), .Load_Dividend(Load_Dividend_into_Q),
    .Load_Sub(Write_Sub_into_R), .Shift_in(Q_Shift_In__Neg), .Counter_plus_plus(output_1_counter_plus_plus),
    .Shift_Q(Shift_Q), .Shift_R(Shift_Remainder), .Done(Done));

  // Notes on the sheet:
  //   decides when to shift the Divisor and Quotient registers and when to write new values into the remainder register
endmodule

module Next_State (
  input  Reset,
  input  State_0_IN,
  input  State_1_IN,
  input  State_2_IN,
  input  State_3_IN,
  input  Counter_Carry,
  output State_0,
  output State_1,
  output State_2,
  output State_3
);

  wire and_1_out, and_3_out, and_4_out, and_5_out, not_1_out;

  not not_1 (not_1_out, Reset);
  and and_1 (and_1_out, State_0_IN, not_1_out);
  and and_2 (State_2, State_1_IN, not_1_out);
  and and_3 (and_3_out, State_2_IN, not_1_out, ~Counter_Carry);  // AND_Gate
  and and_4 (and_4_out, State_3_IN, not_1_out);
  and and_5 (and_5_out, State_2_IN, not_1_out, Counter_Carry);
  or or_1 (State_1, and_1_out, and_3_out);
  or or_2 (State_3, and_5_out, and_4_out);

  assign State_0 = Reset;
endmodule

module Output (
  input  State_0,
  input  Neg,
  input  State_1,
  input  State_2,
  input  Count_Carry,
  input  State_3,
  output Load_Divisor,
  output Load_Dividend,
  output Load_Sub,
  output Shift_in,
  output Counter_plus_plus,
  output Shift_Q,
  output Shift_R,
  output Done
);

  wire not_1_out, not_2_out;

  not not_1 (not_1_out, Neg);
  and and_1 (Load_Sub, not_1_out, State_1);
  not not_2 (not_2_out, Count_Carry);
  and and_2 (Shift_R, State_2, not_2_out);

  assign Counter_plus_plus = State_2;
  assign Done = State_3;
  assign Load_Dividend = State_0;
  assign Load_Divisor = State_0;
  assign Shift_in = Load_Sub;
  assign Shift_Q = State_2;
endmodule

module Div_Rem (
  input  Write_Sub_to_R,
  input  [7:0] Dividend,
  input  [7:0] Sub,
  input  Shift_Q,
  input  Shift_R,
  input  Q_Shift_In,
  input  Load_Div_into_Q,
  input  Reset,
  output [7:0] Quotient,
  output [7:0] Remainder
);

  wire clock_1_out, d_ff_1_q, left_shift_1_shift_out;

  Clock clock_1 (.out(clock_1_out));
  Left_Shift left_shift_1 (
    .Input(Dividend), .Load(Load_Div_into_Q), .Shift_in(d_ff_1_q), .Enable(Shift_Q), .Clear(Reset),
    .Shift_out(left_shift_1_shift_out), .Output(Quotient));
  D_Flip_Flop d_ff_1 (.clk(clock_1_out), .D(Q_Shift_In), .Q(d_ff_1_q));  // open: Qn, preset, en, reset
  Left_Shift left_shift_2 (
    .Input(Sub), .Load(Write_Sub_to_R), .Shift_in(left_shift_1_shift_out), .Enable(Shift_R), .Clear(Reset),
    .Output(Remainder));  // open: Shift_out
endmodule

module Left_Shift (
  input  [7:0] Input,
  input  Load,
  input  Shift_in,
  input  Enable,
  input  Clear,
  output Shift_out,
  output [7:0] Output
);

  wire clock_1_out;

  Clock clock_1 (.out(clock_1_out));
  Shift_Register shift_register_1 (
    .shift(Enable), .in(Shift_in), .clk(clock_1_out), .out(Shift_out), .load(Load), .clr(Clear),
    .d0(Input[0]), .q0(Output[0]), .d1(Input[1]), .q1(Output[1]), .d2(Input[2]), .q2(Output[2]),
    .d3(Input[3]), .q3(Output[3]), .d4(Input[4]), .q4(Output[4]), .d5(Input[5]), .q5(Output[5]),
    .d6(Input[6]), .q6(Output[6]), .d7(Input[7]), .q7(Output[7]));
endmodule
